// Logisim project lab1.circ as structural Verilog: 1 circuit, main circuit main
module main (
  input  x2,
  input  x1,
  input  x0,
  output r
);

  wire and_1_out, and_2_out, and_3_out, not_1_out, not_2_out, not_3_out;

  not not_1 (not_1_out, x1);
  not not_2 (not_2_out, x2);
  not not_3 (not_3_out, x0);
  and and_1 (and_1_out, x2, not_1_out);
  and and_2 (and_2_out, not_2_out, x1);
  or or_1 (r, and_1_out, and_3_out);
  and and_3 (and_3_out, and_2_out, not_3_out);
endmodule
